# Fritzing sketch deviceconnection (saved by Fritzing 0.9.3b)
breadboards: 1

parts:
  Buck_Convertor1 = Buck Convertor [part_number=LM2596 package=THT]
  M1 = BTS7960
  M2 = BTS7960
  Part1 = Adafruit PCA9685 PWM/Servo Breakout [part_number=815]
  DC_Mot_Enc1 = DC Motor with two-phase hall-encoder [part_number=VT-E-G25A-06-177E]
  DC_Mot_Enc2 = DC Motor with two-phase hall-encoder [part_number=VT-E-G25A-06-177E]
  Power_plug1 = Power plug
  J1 = Basic Servo
  J2 = Basic Servo
  J3 = Basic Servo
  Part2 = Arduino Uno (Rev3) - ICSP
  J4 = Basic Servo
  M3 = BTS7960
  M4 = DC Motor
  S1 = Round Pushbutton
  S2 = Round Pushbutton
  Part3 = Arduino Uno (Rev3) - ICSP
  Buck_Convertor2 = Buck Convertor [part_number=LM2596 package=THT]
  Buck_Convertor3 = Buck Convertor [part_number=LM2596 package=THT]

nets:
  N1: Buck_Convertor1.Negative_Input, M1.pin12, M2.pin12, Power_plug1.GND, M3.pin12, Buck_Convertor2.Negative_Input, Buck_Convertor3.Negative_Input
  N2: Buck_Convertor1.Positive_Input, M1.pin11, M2.pin11, Power_plug1.VCC, M3.pin11, Buck_Convertor2.Positive_Input, Buck_Convertor3.Positive_Input
  GND: Buck_Convertor1.Negative_Output, M1.pin8, M2.pin8, Part1.GND, DC_Mot_Enc1.pin2, DC_Mot_Enc2.pin2, J1.gnd, J2.gnd, J3.gnd, Part2.GND, J4.gnd, M3.pin8, Part3.GND, Buck_Convertor2.Negative_Output, Buck_Convertor3.Negative_Output
  N3: Buck_Convertor1.Positive_Output, M3.pin3, M3.pin4, M3.pin7, S1.leg1, S2.leg1, Part3.5V
  N4: M1.pin1, Part2.D4
  N5: M1.pin2, Part2.D6_PWM
  N6: M1.pin3, M1.pin4, Part2.D5_PWM
  N7: M1.pin7, M2.pin7, DC_Mot_Enc1.pin5, DC_Mot_Enc2.pin5, Part2.5V, Buck_Convertor2.Positive_Output
  N8: M1.pin9, DC_Mot_Enc1.pin6
  N9: M1.pin10, DC_Mot_Enc1.pin1
  N10: M2.pin1, Part2.D12/MISO
  N11: M2.pin2, Part2.D10_PWM/SS
  N12: M2.pin3, M2.pin4, Part2.D11_PWM/MOSI
  N13: M2.pin9, DC_Mot_Enc2.pin6
  N14: M2.pin10, DC_Mot_Enc2.pin1
  N15: Part1.PWRIN, Buck_Convertor3.Positive_Output
  N16: Part1.SDA, Part2.A4/SDA, Part3.A4/SDA
  N17: Part1.SCL, Part2.A5/SCL, Part3.A5/SCL
  N18: Part1.PWM15, J1.pulse
  VCC: Part1.5.0V, J1.vcc, J2.vcc, J3.vcc, J4.vcc
  N19: Part1.PWM14, J2.pulse
  N20: Part1.PWM13, J3.pulse
  N21: Part1.PWM12, J4.pulse
  N22: DC_Mot_Enc1.pin3, Part2.D7
  N23: DC_Mot_Enc1.pin4, Part2.D2
  N24: DC_Mot_Enc2.pin3, Part2.D8
  N25: DC_Mot_Enc2.pin4, Part2.D3_PWM
  N26: M3.pin1, Part3.D5_PWM
  N27: M3.pin2, Part3.D6_PWM
  N28: M3.pin9, M4.pin_2
  N29: M3.pin10, M4.pin_1
  N30: S1.leg0, Part3.D2
  N31: S2.leg0, Part3.D3_PWM

custom parts:
  Buck Convertor: DC to DC buck convertor
  BTS7960: BTS7960 43A Peak Power H-Bridge PWM Motor Driver
  Adafruit PCA9685 PWM/Servo Breakout: Using only two pins, control 16 free-running PWM outputs! I2C-controlled PWM driver with a built in clock. Unlike the TLC5940 family, you do not need to continuously send it signal tying up your microcontroller, its completely free running! 5V compliant, which means you can control it from a 3.3V microcontroller and still safely drive up to 6V outputs (this is good for when you want to control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
